// Logisim project CS382_proj2.circ as structural Verilog: 1 circuit, main circuit main
module main (
);

  wire and_1_out, and_2_out, and_3_out, and_4_out, and_5_out, clock_1_out, decoder_1_out0, decoder_1_out1,
       decoder_1_out2, decoder_1_out3, nor_1_out, or_1_out, or_2_out, switch_1_p2;
  wire [1:0] InstructionMemory_dout_3, multiplexer_3_out;
  wire [3:0] bit_extender_1_out, bit_extender_2_out, bit_extender_3_out, bit_extender_4_out,
       bit_extender_5_out, bit_extender_6_out, bit_extender_7_out, bit_extender_8_out,
       InstructionMemory_dout_2, multiplexer_6_out, multiplexer_6_out_2, multiplexer_8_out,
       multiplexer_8_out_2, multiplexer_9_out, multiplexer_9_out_2, PC_q, PC_q_2, Y1_q, Y1_q_2, Y2_q, Y2_q_2,
       Y3_q, Y3_q_2;
  wire [4:0] multiplexer_5_out, multiplexer_10_out, multiplexer_11_out, multiplexer_12_out;
  wire [7:0] adder_1_out, adder_2_out, DataMemory_dout, multiplexer_1_out, multiplexer_2_out,
       multiplexer_4_out, multiplexer_7_out, subtractor_1_out, Y0_q;
  wire [7:6] InstructionMemory_dout;

  Clock clock_1 (.out(clock_1_out));
  // Switch switch_1: pin names not known; wires that end beside it: 1'b1, switch_1_p2
  Adder adder_1 (.a({PC_q_2, PC_q}), .b(8'h1), .out(adder_1_out));  // open: cin, cout
  and and_1 (and_1_out, clock_1_out, switch_1_p2);
  Register PC (.D(adder_1_out), .en(1'b1), .clk(and_1_out), .Q({PC_q_2, PC_q}));  // open: clr
  LedBar Binary_PC_LED_Bar (
    .led0(PC_q_2[3]), .led1(PC_q_2[2]), .led2(PC_q_2[1]), .led3(PC_q_2[0]), .led4(PC_q[3]), .led5(PC_q[2]),
    .led6(PC_q[1]), .led7(PC_q[0]));
  nor nor_1 (nor_1_out, InstructionMemory_dout[7], InstructionMemory_dout[6]);
  or or_1 (or_1_out, InstructionMemory_dout[7], InstructionMemory_dout[6]);
  Multiplexer #(.width(8)) multiplexer_1 (
    .in0(DataMemory_dout), .in1(multiplexer_7_out), .out(multiplexer_1_out), .sel(InstructionMemory_dout[7]));
  DotMatrix #(.matrixcols(8), .matrixrows(1)) Binary_PC_LED (
    .col0(PC_q_2[3]), .col1(PC_q_2[2]), .col2(PC_q_2[1]), .col3(PC_q_2[0]), .col4(PC_q[3]), .col5(PC_q[2]),
    .col6(PC_q[1]), .col7(PC_q[0]));
  Hex_Digit_Display Program (.value(PC_q_2));  // open: dp
  Hex_Digit_Display Counter (.value(PC_q));  // open: dp
  RAM #(.enables("line")) InstructionMemory (
    .addr({PC_q_2, PC_q}), .clk(and_1_out),
    .dout({InstructionMemory_dout, InstructionMemory_dout_3, InstructionMemory_dout_2}));  // open: we, din
  Decoder #(.select(2)) decoder_1 (
    .out0(decoder_1_out0), .out1(decoder_1_out1), .out2(decoder_1_out2), .out3(decoder_1_out3),
    .sel(InstructionMemory_dout_3));  // open: en
  RAM #(.addrWidth(4), .enables("line")) DataMemory (
    .addr(InstructionMemory_dout_2), .we(nor_1_out), .clk(and_1_out), .din(multiplexer_2_out),
    .dout(DataMemory_dout));
  and and_2 (and_2_out, decoder_1_out0, or_1_out);
  and and_3 (and_3_out, decoder_1_out1, or_1_out);
  and and_4 (and_4_out, decoder_1_out2, or_1_out);
  and and_5 (and_5_out, decoder_1_out3, or_1_out);
  Register Y0 (.D(multiplexer_1_out), .en(and_2_out), .clk(and_1_out), .Q(Y0_q));  // open: clr
  Register Y1 (.D(multiplexer_1_out), .en(and_3_out), .clk(and_1_out), .Q({Y1_q_2, Y1_q}));  // open: clr
  Register Y2 (.D(multiplexer_1_out), .en(and_4_out), .clk(and_1_out), .Q({Y2_q_2, Y2_q}));  // open: clr
  Register Y3 (.D(multiplexer_1_out), .en(and_5_out), .clk(and_1_out), .Q({Y3_q_2, Y3_q}));  // open: clr
  Hex_Digit_Display hex_digit_display_1 (.value(bit_extender_1_out));  // open: dp
  Hex_Digit_Display hex_digit_display_2 (.value(bit_extender_2_out));  // open: dp
  assign bit_extender_1_out = {{3{1'b0}}, InstructionMemory_dout[7]};  // Bit_Extender bit_extender_1
  Hex_Digit_Display hex_digit_display_3 (.value(Y0_q[7:4]));  // open: dp
  Hex_Digit_Display hex_digit_display_4 (.value(Y0_q[3:0]));  // open: dp
  or or_2 (or_2_out, InstructionMemory_dout[6], InstructionMemory_dout[7]);
  Hex_Digit_Display hex_digit_display_5 (.value(bit_extender_3_out));  // open: dp
  Hex_Digit_Display hex_digit_display_6 (.value(bit_extender_4_out));  // open: dp
  assign bit_extender_2_out = {{3{1'b0}}, InstructionMemory_dout[6]};  // Bit_Extender bit_extender_2
  Hex_Digit_Display hex_digit_display_7 (.value(Y1_q_2));  // open: dp
  Multiplexer #(.select(2), .width(8)) multiplexer_2 (
    .in0(Y0_q), .in1({Y1_q_2, Y1_q}), .in2({Y2_q_2, Y2_q}), .in3({Y3_q_2, Y3_q}), .out(multiplexer_2_out),
    .sel(multiplexer_3_out));
  Multiplexer #(.width(2)) multiplexer_3 (
    .in0(InstructionMemory_dout_3), .in1(InstructionMemory_dout_2[3:2]), .out(multiplexer_3_out),
    .sel(or_2_out));
  Multiplexer #(.select(2), .width(8)) multiplexer_4 (
    .in0(Y0_q), .in1({Y1_q_2, Y1_q}), .in2({Y2_q_2, Y2_q}), .in3({Y3_q_2, Y3_q}), .out(multiplexer_4_out),
    .sel(InstructionMemory_dout_2[1:0]));
  Hex_Digit_Display hex_digit_display_8 (.value(bit_extender_5_out));  // open: dp
  Hex_Digit_Display hex_digit_display_9 (.value(bit_extender_6_out));  // open: dp
  assign bit_extender_3_out = {{3{1'b0}}, InstructionMemory_dout_3[1]};  // Bit_Extender bit_extender_3
  assign bit_extender_4_out = {{3{1'b0}}, InstructionMemory_dout_3[0]};  // Bit_Extender bit_extender_4
  Hex_Digit_Display hex_digit_display_10 (.value(Y1_q));  // open: dp
  Hex_Digit_Display hex_digit_display_11 (.value(Y2_q_2));  // open: dp
  Hex_Digit_Display hex_digit_display_12 (.value(bit_extender_7_out));  // open: dp
  Hex_Digit_Display hex_digit_display_13 (.value(bit_extender_8_out));  // open: dp
  assign bit_extender_5_out = {{3{1'b0}}, InstructionMemory_dout_2[3]};  // Bit_Extender bit_extender_5
  Hex_Digit_Display hex_digit_display_14 (.value(Y2_q));  // open: dp
  assign bit_extender_6_out = {{3{1'b0}}, InstructionMemory_dout_2[2]};  // Bit_Extender bit_extender_6
  Hex_Digit_Display hex_digit_display_15 (.value(Y3_q_2));  // open: dp
  Hex_Digit_Display hex_digit_display_16 (.value(Y3_q));  // open: dp
  assign bit_extender_7_out = {{3{1'b0}}, InstructionMemory_dout_2[1]};  // Bit_Extender bit_extender_7
  assign bit_extender_8_out = {{3{1'b0}}, InstructionMemory_dout_2[0]};  // Bit_Extender bit_extender_8
  Multiplexer #(.width(5)) multiplexer_5 (
    .in0(multiplexer_10_out), .in1(multiplexer_12_out), .out(multiplexer_5_out),
    .sel(InstructionMemory_dout[6]));
  Hex_Digit_Display hex_digit_display_17 (.value(multiplexer_6_out_2));  // open: dp
  Adder adder_2 (.a(multiplexer_2_out), .b(multiplexer_4_out), .out(adder_2_out));  // open: cin, cout
  Subtractor subtractor_1 (.a(multiplexer_2_out), .b(multiplexer_4_out), .out(subtractor_1_out));  // open: bin, bout
  Hex_Digit_Display hex_digit_display_18 (.value(multiplexer_6_out));  // open: dp
  DotMatrix #(.matrixrows(5)) dotmatrix_1 (
    .col0(multiplexer_12_out), .col1(multiplexer_12_out), .col2(multiplexer_5_out),
    .col3(multiplexer_12_out), .col4(multiplexer_12_out));
  Multiplexer #(.width(8)) multiplexer_6 (
    .in1(multiplexer_2_out), .out({multiplexer_6_out_2, multiplexer_6_out}), .sel(InstructionMemory_dout[7]));  // open: in0
  Multiplexer #(.width(8)) multiplexer_7 (
    .in0(adder_2_out), .in1(subtractor_1_out), .out(multiplexer_7_out), .sel(InstructionMemory_dout[6]));
  Hex_Digit_Display hex_digit_display_19 (.value(multiplexer_8_out_2));  // open: dp
  Hex_Digit_Display hex_digit_display_20 (.value(multiplexer_8_out));  // open: dp
  DotMatrix #(.matrixrows(5)) dotmatrix_2 (
    .col0(multiplexer_11_out), .col1(multiplexer_11_out), .col2(multiplexer_11_out),
    .col3(multiplexer_11_out), .col4(multiplexer_11_out));
  Multiplexer #(.width(8)) multiplexer_8 (
    .in1(multiplexer_4_out), .out({multiplexer_8_out_2, multiplexer_8_out}), .sel(InstructionMemory_dout[7]));  // open: in0
  Hex_Digit_Display hex_digit_display_21 (.value(multiplexer_9_out_2));  // open: dp
  Hex_Digit_Display hex_digit_display_22 (.value(multiplexer_9_out));  // open: dp
  Multiplexer #(.width(8)) multiplexer_9 (
    .in1(multiplexer_7_out), .out({multiplexer_9_out_2, multiplexer_9_out}), .sel(InstructionMemory_dout[7]));  // open: in0
  Multiplexer #(.width(5)) multiplexer_10 (
    .in0({5{1'b0}}), .in1({5{1'b1}}), .out(multiplexer_10_out), .sel(InstructionMemory_dout[7]));
  Multiplexer #(.width(5)) multiplexer_11 (
    .in0({5{1'b0}}), .in1(5'b01010), .out(multiplexer_11_out), .sel(InstructionMemory_dout[7]));
  Multiplexer #(.width(5)) multiplexer_12 (
    .in0({5{1'b0}}), .in1(5'b00100), .out(multiplexer_12_out), .sel(InstructionMemory_dout[7]));

  // Notes on the sheet:
  //   Names: Alexander Francese & Milind Kathiari
  //   Pledge: I pledge my honor that I have abided by the Stevens Honor System.
  //   CPU Name: Maffamatix Masheen
  //   Mr. Clock
  //   Make sure switch is set to *ON*
  //   before you start the simulation
  //   RegDataW
  //   WriteReg
  //   RegWrite
  //   Y0
  //   Current Instruction:
  //   Y1
  //   ReadReg1
  //   ReadReg2
  //   Y2
  //   Y3
  //   RegData1
  //   RegData2
  //   ALU
  //   Maffamatix
endmodule
